// Logisim project 8 bit LE register.circ as structural Verilog: 1 circuit, main circuit main
module main (
  input  [7:0] in_1,
  input  LE,
  input  Reset,
  output [7:0] out_4
);

  wire clock_1_out, multiplexer_1_out, multiplexer_2_out, multiplexer_3_out, multiplexer_4_out,
       multiplexer_5_out, multiplexer_6_out, multiplexer_7_out, multiplexer_8_out;

  Clock clock_1 (.out(clock_1_out));
  Multiplexer #(.enable("false")) multiplexer_1 (.in0(out_4[0]), .in1(in_1[0]), .out(multiplexer_1_out), .sel(LE));
  D_Flip_Flop d_ff_1 (
    .clk(clock_1_out), .D(multiplexer_1_out), .Q(out_4[0]), .en(1'b1), .reset(Reset));  // open: Qn, preset
  Multiplexer #(.enable("false")) multiplexer_2 (.in0(out_4[1]), .in1(in_1[1]), .out(multiplexer_2_out), .sel(LE));
  D_Flip_Flop d_ff_2 (
    .clk(clock_1_out), .D(multiplexer_2_out), .Q(out_4[1]), .en(1'b1), .reset(Reset));  // open: Qn, preset
  Multiplexer #(.enable("false")) multiplexer_3 (.in0(out_4[2]), .in1(in_1[2]), .out(multiplexer_3_out), .sel(LE));
  D_Flip_Flop d_ff_3 (
    .clk(clock_1_out), .D(multiplexer_3_out), .Q(out_4[2]), .en(1'b1), .reset(Reset));  // open: Qn, preset
  Multiplexer #(.enable("false")) multiplexer_4 (.in0(out_4[3]), .in1(in_1[3]), .out(multiplexer_4_out), .sel(LE));
  D_Flip_Flop d_ff_4 (
    .clk(clock_1_out), .D(multiplexer_4_out), .Q(out_4[3]), .en(1'b1), .reset(Reset));  // open: Qn, preset
  Multiplexer #(.enable("false")) multiplexer_5 (.in0(out_4[4]), .in1(in_1[4]), .out(multiplexer_5_out), .sel(LE));
  D_Flip_Flop d_ff_5 (
    .clk(clock_1_out), .D(multiplexer_5_out), .Q(out_4[4]), .en(1'b1), .reset(Reset));  // open: Qn, preset
  Multiplexer #(.enable("false")) multiplexer_6 (.in0(out_4[5]), .in1(in_1[5]), .out(multiplexer_6_out), .sel(LE));
  D_Flip_Flop d_ff_6 (
    .clk(clock_1_out), .D(multiplexer_6_out), .Q(out_4[5]), .en(1'b1), .reset(Reset));  // open: Qn, preset
  Multiplexer #(.enable("false")) multiplexer_7 (.in0(out_4[6]), .in1(in_1[6]), .out(multiplexer_7_out), .sel(LE));
  D_Flip_Flop d_ff_7 (
    .clk(clock_1_out), .D(multiplexer_7_out), .Q(out_4[6]), .en(1'b1), .reset(Reset));  // open: Qn, preset
  Multiplexer #(.enable("false")) multiplexer_8 (.in0(out_4[7]), .in1(in_1[7]), .out(multiplexer_8_out), .sel(LE));
  D_Flip_Flop d_ff_8 (
    .clk(clock_1_out), .D(multiplexer_8_out), .Q(out_4[7]), .en(1'b1), .reset(Reset));  // open: Qn, preset

  // Notes on the sheet:
  //   Data-in
  //   Data out
endmodule
