// Logisim project DDCA project.circ as structural Verilog: 1 circuit, main circuit main
module main (
  input  I1,
  input  I2,
  input  I3,
  input  I4,
  output out_5
);

  wire _1_out, _2_out, _3_out, _4_out;

  xnor _1 (_1_out, 1'b1, I1);
  xnor _2 (_2_out, 1'b1, I2);
  xnor _3 (_3_out, 1'b0, I3);
  xnor _4 (_4_out, 1'b0, I4);
  and and_1 (out_5, _1_out, _2_out, _3_out, _4_out);

  // Notes on the sheet:
  //   C1
  //   C2
  //   C3
  //   C4
  //   4 bit digital access/verification system using XNOR gate
  //   IF ACCESS = 1, THEN USER CODE=STORED CODE
  //   Access/AND
  //   IF ACCESS=0 , THEN THE USER CODE IS NOT = STORED CODE
endmodule
